# Fritzing sketch Radio (saved by Fritzing 0.9.0b)
breadboards: 1

parts:
  R3 = Resistor [tolerance=±5% resistance=1k package=THT]  # not connected
  Q1 = Basic FET P-Channel [package="TO220 [THT]"]
  V2 = DC Power [voltage=5]  # not connected
  74HCT1 = 74HCT02 [part_number=CD4048B package="DIP (Dual Inline) [THT]"]
  R10 = Resistor [tolerance=±5% resistance=3.3k package=THT]
  R11 = Resistor [tolerance=±5% resistance=2.2k package=THT]
  R12 = Resistor [tolerance=±5% resistance=3.3k package=THT]
  J2 = Screw terminal - 2 pins [package=THT]
  Raspberry_Pi_B_rev1 = Raspberry Pi B rev1
  TPA2016D1 = TPA2016D2 [part_number=TPA2016D2 package="DIP (Dual Inline) [THT]"]
  Volume = Rotary Encoder [package=THT]
  Selection = Rotary Encoder [package=THT]

nets:
  N1: Q1.gate, 74HCT1.1Y
  5V: Q1.drain, Raspberry_Pi_B_rev1.5V, TPA2016D1.VDD
  N2: Q1.source, J2.pin1, Volume.PushA
  N3: 74HCT1.1A, R10.Pin_1, R11.Pin_0, Raspberry_Pi_B_rev1.GPIO_24
  N4: 74HCT1.1B, R12.Pin_1, Raspberry_Pi_B_rev1.GPIO_25
  GND: R10.Pin_0, R12.Pin_0, J2.pin2, Raspberry_Pi_B_rev1.GND, TPA2016D1.GND
  N5: R11.Pin_1, Volume.PushB
  N6: Raspberry_Pi_B_rev1.3V3, TPA2016D1.I2C_VCC, Volume.EncoderPinC, Selection.EncoderPinC
  N7: Raspberry_Pi_B_rev1.GPIO_0, TPA2016D1.SDA
  N8: Raspberry_Pi_B_rev1.GPIO_1, TPA2016D1.SCL
  N9: Raspberry_Pi_B_rev1.GPIO_17, Selection.EncoderPinB
  N10: Raspberry_Pi_B_rev1.GPIO_4, Selection.EncoderPinA
  N11: Raspberry_Pi_B_rev1.GPIO_10, Volume.EncoderPinA
  N12: Raspberry_Pi_B_rev1.GPIO_9, Volume.EncoderPinB

custom parts:
  74HCT02: Quad 2-input TTL NOR gate
  TPA2016D2: Stereo 2.8W Class D Audio Amplifier - I2C Control AGC
  Rotary Encoder: Rotary Encoder from ALPS STEC12E07.
